# Fritzing sketch schema 2 (saved by Fritzing 0.9.3b)
circuit board: 17.278cm x 16.0613cm

parts:
  SparkFun_OpenScale1 = openScale_v04 [part_number=SEN-13261]
  R2 = Resistor [tolerance=±5% resistance=150k package=THT]
  R3 = Resistor [tolerance=±5% resistance=150k package=THT]
  ANT1 = Antenna
  J$1 = SMA Antenna Connector [package=sma-edge]
  U1 = U.FL [package=u.fl]
  S4 = Toggle Switch [package=THT]
  U2 = LIPO-1000mAh [package=lipo-1000]
  Součástka2 = USB LiPoly Charger
  R5 = Resistor [tolerance=±5% resistance=150k package=THT]
  R6 = Resistor [tolerance=±5% resistance=150k package=THT]
  Arduino_MKRFox1200 = Arduino MKR Fox 1200
  JP1 = Jumper [package=sj_2s-no]
  JP2 = Jumper [package=sj_2s-no]
  VCC1 = Battery
  R7 = Resistor [tolerance=±5% resistance=220 package="0402 [SMD]"]
  R8 = Resistor [tolerance=±5% resistance=220 package="0402 [SMD]"]
  R9 = Resistor [tolerance=±5% resistance=220 package="0402 [SMD]"]
  R10 = Resistor [tolerance=±5% resistance=220 package="0402 [SMD]"]
  J1 = Camdenboss CTB0158-2 [part_number=CTB0158-2 package=THT]
  DHT22 = Humidity and Temperature Sensor RHT03
  R11 = Resistor [tolerance=±5% resistance=47k package=THT]
  R12 = Resistor [tolerance=±5% resistance=47k package=THT]
  R13 = PHOTOCELL [package=photocell-kit]
  R14 = Resistor [tolerance=±5% resistance=1k package="0805 [SMD]"]
  R15 = Resistor [tolerance=±5% resistance=1k package="0805 [SMD]"]
  R16 = Resistor [tolerance=±5% resistance=150k package=THT]
  R17 = Resistor [tolerance=±5% resistance=150k package=THT]
  Q2 = Basic FET N-Channel [package="TO220 [THT]"]
  Q1 = Basic FET N-Channel [package="TO220 [THT]"]

nets:
  N1: SparkFun_OpenScale1.AVDD, R7.Pin_0, R8.Pin_1
  GND: SparkFun_OpenScale1.GND, R3.Pin_1, S4.L2, R6.Pin_1, Arduino_MKRFox1200.GND, VCC1.-, R9.Pin_0, R10.Pin_1, DHT22.GND_1, DHT22.GND_2, R17.Pin_1
  N2: SparkFun_OpenScale1.A+, R7.Pin_1, R10.Pin_0, J1.pin2
  N3: SparkFun_OpenScale1.A-, R8.Pin_0, R9.Pin_1, J1.pin1
  5V: SparkFun_OpenScale1.5V, S4.COM, U2.+, Součástka2.VBAT, R5.Pin_0, DHT22.Vcc, R12.Pin_0, R13.P$1, R14.Pin_0, Q2.source
  N4: SparkFun_OpenScale1.TXD, JP2.1
  N5: SparkFun_OpenScale1.RXD, JP1.1
  N6: R2.Pin_0, JP2.2
  N7: R2.Pin_1, R3.Pin_0, Arduino_MKRFox1200.13/RX
  GND_2: ANT1.antenna_lead, J$1.GND, J$1.SIGNAL, U1.GND
  N8: S4.L1, U2.-, Součástka2.GND
  N9: R5.Pin_1, R6.Pin_0, Arduino_MKRFox1200.A2
  N10: Arduino_MKRFox1200.DAC/A0, Arduino_MKRFox1200.VCC, VCC1.+, R11.Pin_1, Q1.gate
  N11: Arduino_MKRFox1200.A6, R16.Pin_1, R17.Pin_0
  N12: Arduino_MKRFox1200.D2_PWM, R12.Pin_1, Q1.source
  N13: Arduino_MKRFox1200.14/TX, Q2.gate
  N14: JP1.2, Q2.drain
  N15: DHT22.Data-signal, R11.Pin_0, Q1.drain
  N16: R13.P$2, R14.Pin_1, R15.Pin_0, R16.Pin_0

notes:
  Light dependent resistor module

custom parts:
  openScale_v04: OpenScale is an open source hardware load cell reader and calibration device. It has the ability to read multiple types of load cells and offers a simple to use serial menu to configure calibration value, sample rate, time stamp, and units of precision.
